# Fritzing sketch midi_hold (saved by Fritzing 0.9.9b)
circuit board: 5.36514cm x 7.14954cm
circuit board: 6.55843cm x 6.1914cm
breadboards: 1

parts:
  RE2 = KY-040 Rotary encoder [package=THT]
  RE1 = KY-040 Rotary encoder [package=THT]
  DIN1 = DIN-5 jack (MIDI) [package=THT]
  R2 = Resistor [tolerance=±5% resistance=220 package="0805 [SMD]"]
  R3 = Resistor [tolerance=±5% resistance=220 package="0805 [SMD]"]
  Part1 = Arduino Nano (Rev3.0) (ICSP)
  Power_plug1 = Power plug
  Grove2 = Grove 4 Digit Display

nets:
  N1: RE2.GND, Part1.D12/MISO
  N2: RE2.Vcc, Part1.D10
  N3: RE2.SW, Part1.D9
  N4: RE2.DT, Part1.D8
  N5: RE2.CLK, Part1.D7
  N6: RE1.GND, Part1.D6
  N7: RE1.Vcc, Part1.D5
  N8: RE1.SW, Part1.D4
  N9: RE1.DT, RE1.CLK, Part1.D2, Part1.D3
  N10: DIN1.5, R3.Pin_0, R3.Pin_1, Part1.D1/TX
  GND: DIN1.2, Part1.GND, Power_plug1.GND, Grove2.GND
  N11: DIN1.4, R2.Pin_0, R2.Pin_1, Part1.5V
  N12: Part1.D11/MOSI, Grove2.5V
  VIN: Part1.VIN, Power_plug1.VCC
  N13: Part1.A1, Grove2.DIO
  N14: Part1.A0, Grove2.CLK

custom parts:
  KY-040 Rotary encoder: KY-040 Rotary Encoder with switch on breakout borad from AZ Delivery
  Grove 4 Digit Display: A 4 7-seg display
